# Fritzing sketch Class_Task (saved by Fritzing 0.9.3b)
circuit board: 8.46667cm x 5.64444cm
breadboards: 1
stripboards: 1
perfboards: 1

parts:
  DHT22 = Humidity and Temperature Sensor RHT03
  BUZZER = Piezo Speaker
  Relay = RELAY [package=relay-jzc]
  Power = Power plug
  Part1 = ESP-WROOM-32 [ESP-32S] Module [part_number=ESP-WROOM-32]
  I2C_Adapter = Adafruit PCF8574 [part_number="Adafruit #5545"]
  U1 = LCD-16X2 [package=lcd-8x2-kit]
  Buck_Converter = RioRand LM2596
  KEYPAD = Keypad Membran 4x4
  LED_INDICATOR = LED indicator 22mm

nets:
  3v3: DHT22.Vcc, I2C_Adapter.VCC, Buck_Converter.Pin_3
  GPIO_32: DHT22.Data-signal, Part1.IO32
  GND: DHT22.GND_2, BUZZER.pin1, Relay.COIL2, Power.GND, Part1.RST, I2C_Adapter.GND, I2C_Adapter.A0, Buck_Converter.Pin_2, Buck_Converter.Pin_4, LED_INDICATOR.Pin_2
  NO: BUZZER.pin2, Relay.NO, LED_INDICATOR.Pin_1
  +24v: Relay.MAIN, Power.VCC, Buck_Converter.Pin_1
  GPIO_5: Relay.COIL1, Part1.IO5
  GPIO_33: Part1.IO33, KEYPAD.Pin7
  GPIO_25: Part1.IO25, KEYPAD.Pin6
  GPIO_26: Part1.IO26, KEYPAD.Pin5
  GPIO_27: Part1.IO27, KEYPAD.Pin4
  GPIO_14: Part1.IO14, KEYPAD.Pin3
  GPIO_12: Part1.IO12, KEYPAD.Pin2
  GPIO_13: Part1.IO13, KEYPAD.Pin1
  GPIO_15: Part1.IO15, KEYPAD.Pin8
  GPIO_21: Part1.IO21, I2C_Adapter.SDA
  GPIO_22: Part1.IO22, I2C_Adapter.SCL
  P0/P1/P2/P7: I2C_Adapter.P0, I2C_Adapter.P1, I2C_Adapter.P2, I2C_Adapter.P7, U1.RS, U1.R_W, U1.E, U1.DB7
  P4: I2C_Adapter.P4, U1.DB4
  P5: I2C_Adapter.P5, U1.DB5
  P6: I2C_Adapter.P6, U1.DB6

custom parts:
  ESP-WROOM-32 [ESP-32S] Module: Espressif ESP-WROOM-32 WiFi/Bluetooth LE microcontroller module also known as the Ai-Thinker ESP-32S module with similar formfactor. The ESP32 is a microcontroller chip with WiFi and BLE capabilities. The chip is developed by Espressif and is the successor to the popular ESP8266 WiFi module.
  Adafruit PCF8574: Expand your project possibilities, with the Adafruit PCF8574 GPIO Expander Breakout - an affordable 8 channel I2C expander. GPIO expanders work like this: you have a board with some number of GPIO but not enough for your project - maybe you need more buttons or LEDs. You could upgrade to a board with massive number of GPIO like the Grand Central, or you could pop on one of these boards.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
  Keypad Membran 4x4: Membrane Keypad 4x4 Matrix
  LED indicator 22mm: AD16-22DS Indicator LED Power Light 22mm.

// code stored in the sketch: code1.ino
// ================================================================
// MDPS374 - Control Room Environmental Monitoring & Alarm System
// ESP32-WROOM-32
// DHT22 on GPIO32
// LCD 16x2 via PCF8574 I2C (SDA=GPIO21, SCL=GPIO22)
// Relay (24V Buzzer) on GPIO5
// ================================================================

#include <Arduino.h>
#include <DHT.h>
#include <LiquidCrystal_I2C.h>

// ?? Pin Definitions ?????????????????????????????????????????????
#define DHTPIN     32
#define DHTTYPE    DHT22
#define RELAY_PIN  5

// ?? DHT Setup ???????????????????????????????????????????????????
DHT dht(DHTPIN, DHTTYPE);

// ?? LCD Setup ???????????????????????????????????????????????????
LiquidCrystal_I2C lcd(0x27, 16, 2);

// ?? Software EMA Low-Pass Filter ????????????????????????????????
float alpha        = 0.1;
float filteredTemp = 0.0;
float filteredHum  = 0.0;
bool  firstReading = true;

float applyEMA(float newVal, float prevFiltered) {
  return (alpha * newVal) + ((1.0 - alpha) * prevFiltered);
}

// ?? Setpoints (fixed, no keypad) ????????????????????????????????
float Tset = 30.0;
float Hset = 70.0;

// ?? State Variables ?????????????????????????????????????????????
bool  alarmActive         = false;
unsigned long alarmStartTime  = 0;
unsigned long lastReadTime    = 0;
unsigned long lastDisplayTime = 0;

// ?? Custom Degree Symbol ????????????????????????????????????????
byte degreeSymbol[8] = {
  0b00110,
  0b01001,
  0b01001,
  0b00110,
  0b00000,
  0b00000,
  0b00000,
  0b00000
};

// ================================================================
void setup() {
  Serial.begin(115200);

  pinMode(RELAY_PIN, OUTPUT);
  digitalWrite(RELAY_PIN, LOW);

  lcd.init();
  lcd.backlight();
  lcd.createChar(0, degreeSymbol);

  dht.begin();

  // Startup message
  lcd.setCursor(0, 0);
  lcd.print("Control Room Mon");
  lcd.setCursor(0, 1);
  lcd.print("  Initializing  ");
  delay(2000);
  lcd.clear();

  Serial.println("System Started.");
}

// ================================================================
// Display: Main Screen
// Row 0: T:XX.X°C H:XX.X%
// Row 1: Ts:XX Hs:XX [status]
// ================================================================
void displayMain() {
  if (millis() - lastDisplayTime < 500) return;
  lastDisplayTime = millis();

  // Row 0 ? Live readings
  lcd.setCursor(0, 0);
  lcd.print("T:");
  lcd.print(filteredTemp, 1);
  lcd.write(byte(0));
  lcd.print("C H:");
  lcd.print(filteredHum, 1);
  lcd.print("%");

  // Row 1 ? Setpoints and status
  lcd.setCursor(0, 1);
  if (alarmActive) {
    lcd.print("!! ALARM ACTIVE!");
  } else {
    lcd.print("Ts:");
    lcd.print(Tset, 0);
    lcd.print(" Hs:");
    lcd.print(Hset, 0);
    lcd.print("% OK");
  }
}

// ================================================================
void loop() {
  unsigned long now = millis();

  // ?? 1. Read DHT22 every 2 seconds ?????????????????????????????
  if (now - lastReadTime >= 2000) {
    lastReadTime = now;

    float rawTemp = dht.readTemperature();
    float rawHum  = dht.readHumidity();

    if (!isnan(rawTemp) && !isnan(rawHum)) {
      if (firstReading) {
        filteredTemp = rawTemp;
        filteredHum  = rawHum;
        firstReading = false;
      } else {
        filteredTemp = applyEMA(rawTemp, filteredTemp);
        filteredHum  = applyEMA(rawHum,  filteredHum);
      }

      // Serial monitor debug
      Serial.print("Raw->  T: ");    Serial.print(rawTemp);
      Serial.print("C  H: ");        Serial.print(rawHum);
      Serial.println("%");
      Serial.print("Filt-> T: ");    Serial.print(filteredTemp);
      Serial.print("C  H: ");        Serial.print(filteredHum);
      Serial.println("%");
      Serial.println("??????????????");

    } else {
      Serial.println("DHT22 read failed! Check wiring.");
    }
  }

  // ?? 2. Alarm Logic ????????????????????????????????????????????
  if (!alarmActive) {
    if (filteredTemp > Tset || filteredHum > Hset) {
      alarmActive    = true;
      alarmStartTime = now;
      digitalWrite(RELAY_PIN, HIGH);
      Serial.println("ALARM TRIGGERED!");
    }
  } else {
    if (now - alarmStartTime >= 10000) {
      alarmActive = false;
      digitalWrite(RELAY_PIN, LOW);
      Serial.println("Alarm cleared.");
    }
  }

  // ?? 3. Update Display ?????????????????????????????????????????
  displayMain();
}
